# Fritzing sketch led-connection-board (saved by Fritzing 0.9.3b)
circuit board: 5.1322cm x 2.17991cm
perfboards: 1

parts:
  R2 = Resistor [tolerance=±5% resistance=1.8 package=THT]
  R1 = Resistor [tolerance=±5% resistance=1.8 package=THT]
  J2 = male alternating pin header, 3 pins [form="♂ (male)"]
  J1 = male pin header, 6 pins [form="♂ (male)"]
  R3 = Resistor [tolerance=±5% resistance=4.7k package=THT]
  Q1_-_2N3904 = NPN-Transistor [package="TO92 [THT]"]

nets:
  N1: R2.Pin_0, J2.pin1
  3.3V: R2.Pin_1, R1.Pin_1, J1.pin1, J1.pin2
  N2: R1.Pin_0, J2.pin2
  N3: J2.pin3, R3.Pin_1
  GND: J1.pin3, J1.pin4, Q1_-_2N3904.E
  N4: J1.pin5, J1.pin6, Q1_-_2N3904.C
  N5: R3.Pin_0, Q1_-_2N3904.B

notes:
  Dulciurilla, Connection board for the LED lights, 1
  LED 1 +
  LED 2 +
  GPIO Pin
  LED 1 -
  LED 2 -
  3.3V
  GND
  GPIO
  J1
  J2
